# Fritzing sketch Bot Circuit Diagram V1 (saved by Fritzing 0.9.3b)
breadboards: 1

parts:
  Raspberry_Pi_1 = Raspberry Pi 4 [part_number=RPI-4-b]
  Part1 = Adafruit VL6180X Time of Flight Distance Sensor [part_number="Adafruit #3316"]
  Part2 = Adafruit VL6180X Time of Flight Distance Sensor [part_number="Adafruit #3316"]
  Part3 = Adafruit TCA9548A
  IC1 = Rasberry Pi NIOR Camera [chip_label=IC package="DIP (Dual Inline) [THT]"]  # not connected
  GY1 = MPU-6050 Board GY-521 [form="♀ (female)" package=THT]
  Part8 = Arduino Pro Mini v13
  Part9 = Arduino Pro Mini v13
  J1 = Basic Servo
  J2 = Basic Servo
  J3 = Basic Servo
  J4 = Basic Servo
  J5 = Basic Servo
  Part10 = Lilypad Battery Connect
  USBUART1 = CP2102 USB UART Breakout
  USBUART2 = CP2102 USB UART Breakout

nets:
  GND: Raspberry_Pi_1.GND, Part1.GND, Part2.GND, Part3.GND, GY1.pin2, Part8.GND, Part9.GND, J1.gnd, J2.gnd, J3.gnd, J4.gnd, J5.gnd, Part10.-, USBUART1.GND, USBUART2.GND
  VCC: Raspberry_Pi_1.5V, Part1.VIN, Part2.VIN, Part3.VCC, GY1.pin1, Part8.VCC, Part9.VCC, J1.vcc, J2.vcc, J3.vcc, J4.vcc, J5.vcc, Part10.+, USBUART1.VCCIO, USBUART2.VCCIO
  N1: Part1.SCL, Part3.4SCL
  N2: Part1.SDA, Part3.4SDA
  N3: Part2.SCL, Part3.5SCL
  N4: Part2.SDA, Part3.5SDA
  N5: Part3.INPUTSDA, Part8.A4
  N6: Part3.INPUTSCL, Part8.A5
  N7: GY1.pin3, Part9.A5
  N8: GY1.pin4, Part9.A4
  N9: Part8.D0/TX, USBUART1.RXD
  N10: Part8.D1/RX, USBUART1.TXD
  N11: Part8.D6_PWM, J4.pulse
  N12: Part8.D5_PWM, J5.pulse
  N13: Part9.D0/TX, USBUART2.RXD
  N14: Part9.D1/RX, USBUART2.TXD
  N15: Part9.D6_PWM, J3.pulse
  N16: Part9.D5_PWM, J2.pulse
  N17: Part9.D3_PWM, J1.pulse

notes:
  Battery
  To USB
  Continous Rotation Servos
  Ear
  Torso
  Gyroscope
  MCU1
  MCU2
  RPI 4 8GB
  To Display
  ToF Sensors

custom parts:
  Raspberry Pi 4: The RPi4, a faster version of the awesome Raspberry Pi 2 B ARM Board with 40 pin gpio. Ready for special Raspberry Pi B+ and RPi2 Hat (Hardware attached (on) top)
  Adafruit VL6180X Time of Flight Distance Sensor: The VL6180X is a Time of Flight distance sensor like no other you've used! The sensor contains a very tiny invisible laser source, and a matching sensor. The VL6180X can detect the "time of flight", or how long the light has taken to bounce back to the sensor. Since it uses a very narrow light source, it is good for determining distance of only the surface directly in front of it. Unlike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
  Adafruit TCA9548A: You just found the perfect I2C sensor, and you want to wire up two or three or more of them to your Arduino when you realize "Uh oh, this chip has a fixed I2C address, and from what I know about I2C, you cannot have two devices with the same address on the same SDA/SCL pins!" Are you out of luck? You would be, if you didn't have this ultra-cool TCA9548A 1-to-8 I2C multiplexer! Finally, a way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
  Rasberry Pi NIOR Camera: Camera
  MPU-6050 Board GY-521: Acelerometro y Giroscopio MPU-6050 Board GY-521
  CP2102 USB UART Breakout: CP2102 Usb Uart Breakout Board with Battery
